# Fritzing sketch BlueRCCar (saved by Fritzing 0.9.3b)
stripboards: 1

parts:
  U1 = attiny85 [package=dip]
  BT1 = Bluetooth HC-06u [package=THT]
  R1 = Resistor [tolerance=±5% resistance=10k package=THT]
  U2_VCC = Header 1 [package=1x01_offset]
  U2_GND = Header 1 [package=1x01_offset]
  U2_SDA = Header 1 [package=1x01_offset]
  U2_SCL = Header 1 [package=1x01_offset]
  R2 = Resistor [tolerance=±5% resistance=1k package=THT]
  R3 = Resistor [tolerance=±5% resistance=2.2k package=THT]
  U2_D0 = Header 1 [package=1x01_offset]
  U2_D1 = Header 1 [package=1x01_offset]
  U2_D2 = Header 1 [package=1x01_offset]
  U2_D3 = Header 1 [package=1x01_offset]
  U2_D4 = Header 1 [package=1x01_offset]
  U2_D5 = Header 1 [package=1x01_offset]
  U2_D6 = Header 1 [package=1x01_offset]
  U2_D7 = Header 1 [package=1x01_offset]  # not connected
  Q1 = Basic FET P-Channel [part_number=BS250 package="TO220 [THT]"]
  Q2 = Basic FET P-Channel [part_number=BS250 package="TO220 [THT]"]
  Q3 = Basic FET P-Channel [part_number=BS250 package="TO220 [THT]"]
  Q4 = Basic FET P-Channel [part_number=BS250 package="TO220 [THT]"]
  C2 = Tantalum Capacitor [capacitance=10µF package="100 mil [THT, tantalum]"]
  LED1 = LED - 5mm [color="Yellow (595nm)" package="5 mm [THT]"]
  LED2 = LED - 5mm [color="Yellow (595nm)" package="5 mm [THT]"]
  R4 = Resistor [tolerance=±5% resistance=220 package=THT]
  LED3 = LED - 5mm [color="Red (633nm)" package="5 mm [THT]"]
  LED4 = LED - 5mm [color="Red (633nm)" package="5 mm [THT]"]
  R5 = Resistor [tolerance=±5% resistance=220 package=THT]
  U2 = Battery Holders [package=lipo-1100mAh]

nets:
  N1: U1.Pin_1, R1.Pin_0
  N2: U1.Pin_2, R2.Pin_1
  N3: U1.Pin_3, BT1.TXD
  GND: U1.Pin_4, BT1.GND, U2_GND.1, R3.Pin_0, C2.-, U2.-
  N4: U1.Pin_5, U2_SDA.1
  N5: U1.Pin_7, U2_SCL.1
  5V: U1.Pin_8, BT1.VCC, R1.Pin_1, U2_VCC.1, Q1.source, C2.+, R4.Pin_0, R5.Pin_0, U2.+
  N6: BT1.RXD, R2.Pin_0, R3.Pin_1
  N7: U2_D0.1, Q1.gate
  N8: U2_D1.1, Q2.gate
  N9: U2_D2.1, Q3.gate
  N10: U2_D3.1, Q4.gate
  Front Light: U2_D4.1, LED2.cathode
  Rear Light: U2_D5.1, LED4.cathode
  Horn: U2_D6.1
  Forward: Q1.drain
  Backward: Q2.drain
  N11: Q2.source, Q3.source, Q4.source
  Left: Q3.drain
  Right: Q4.drain
  N12: LED1.cathode, LED2.anode
  N13: LED1.anode, R4.Pin_1
  N14: LED3.cathode, LED4.anode
  N15: LED3.anode, R5.Pin_1

notes:
  PCF8574
  Breakout
  U2

custom parts:
  Bluetooth HC-06u: Bluetooth HC-06 - face up, pins down 16.5mm x 37.5mm PCB
